# Fritzing sketch esp8266 (saved by Fritzing 0.9.3b)
breadboards: 1

parts:
  ESP8266 = ESP8266 WiFi Module [part_number=ESP8266]
  STM32_Blue_Pill = STM32F103C8T6 blue mini board [package=LQFP-48]

nets:
  N1: ESP8266.RXD, STM32_Blue_Pill.A2
  VCC: ESP8266.VCC, STM32_Blue_Pill.3.3V, STM32_Blue_Pill.3.3
  N2: ESP8266.GND, STM32_Blue_Pill.G
  N3: ESP8266.TXD, STM32_Blue_Pill.A3

notes:
  UART2
  rx2 tx2
  ESP8266
  rxd vcc
  gnd txd

custom parts:
  ESP8266 WiFi Module: Generic WiFi Module based on the ESP8266 with onboard PCB antenna and UART communications
  STM32F103C8T6 blue mini board: Generic Blue Pill microcomputer module, available from Ebay and others. CPU STM32F103C8 72Mhz Flash: 64 KB/128 KB RAM: 20KB.
